# Fritzing sketch Traffic_Light (saved by Fritzing 0.9.0b)
breadboards: 1

parts:
  R1 = Resistor [tolerance=±5% resistance=330 package=THT]
  LED1 = LED - 5mm [color="Red (633nm)" package="5 mm [THT]"]
  LED2 = LED - 5mm [color="Yellow (595nm)" package="5 mm [THT]"]
  LED3 = LED - 5mm [color="Green (570nm)" package="5 mm [THT]"]
  LED4 = LED - 5mm [color="Red (633nm)" package="5 mm [THT]"]
  LED5 = LED - 5mm [color="Yellow (595nm)" package="5 mm [THT]"]
  LED6 = LED - 5mm [color="Green (570nm)" package="5 mm [THT]"]
  R2 = Resistor [tolerance=±5% resistance=330 package=THT]
  S2 = Pushbutton [package="[THT]"]
  R4 = Rotary Potentiometer (Small) [maximum_resistance=100kΩ package=THT]
  Arduino1 = Arduino Uno (Rev3)

nets (from the breadboard view):
  N1: R1.Pin_0, LED1.cathode, LED2.cathode, LED3.cathode
  N2: R1.Pin_1, R2.Pin_0, S2.Pin_3, S2.Pin_4, R4.leg1, Arduino1.GND
  N3: LED1.anode, Arduino1.D13/SCK
  N4: LED2.anode, Arduino1.D12/MISO
  N5: LED3.anode, Arduino1.D11_PWM/MOSI
  N6: LED4.cathode, LED5.cathode, LED6.cathode, R2.Pin_1
  N7: LED4.anode, Arduino1.D10_PWM/SS
  N8: LED5.anode, Arduino1.D9_PWM
  N9: LED6.anode, Arduino1.D8
  N10: S2.Pin_1, S2.Pin_2, Arduino1.D7
  N11: R4.wiper, Arduino1.A0
  N12: R4.leg2, Arduino1.5V

notes:
  Copyright 2013-2014 Rob Purser
  Fun with Arduino by Rob Purser is licensed under a
  Creative Commons
  Attribution-NonCommercial-ShareAlike 3.0 Unported License.
  Based on a work at http://www.funwitharduino.net
