# Fritzing sketch Battery_Powered (saved by Fritzing 0.9.0b)
breadboards: 1

parts:
  Part2 = Digital Temperature Sensor Breakout - TMP102
  U1 = mystery part, 5 pins [chip_label=HH10D]
  R4 = Resistor [tolerance=±5% resistance=330 package=THT]
  R5 = Resistor [tolerance=±5% resistance=330 package=THT]
  R6 = Resistor [tolerance=±5% resistance=330 package=THT]
  LED2 = RGB LED - (4 legs) [package="5 mm [THT]"]
  U2 = mystery part, 6 pins [chip_label=MPL3115A2]
  S1 = Pushbutton [package="[THT]"]
  Part3 = NCP1400 Step-Up Breakout
  VCC2 = Battery
  part = NCP1400 Step-Up Breakout  # not connected
  Part1 = Arduino Uno (Rev3)

nets:
  3.3V: Part2.V+, U1.pin2, U2.pin5, Part1.3V3
  N1: Part2.SDA, U1.pin4, U2.pin3, Part1.A4/SDA
  N2: Part2.SCL, U1.pin5, U2.pin4, Part1.A5/SCL
  GND: Part2.GND, Part2.ADD0, U1.pin1, LED2.common_anode, U2.pin6, S1.Pin_3, S1.Pin_4, Part3.GND, VCC2.-, Part1.GND
  N3: U1.pin3, Part1.D3_PWM
  N4: R4.Pin_0, LED2.blue_cathode
  N5: R4.Pin_1, Part1.D5_PWM
  N6: R5.Pin_0, LED2.green_cathode
  N7: R5.Pin_1, Part1.D6_PWM
  N8: R6.Pin_0, LED2.red_cathode
  N9: R6.Pin_1, Part1.D9_PWM
  N10: S1.Pin_1, S1.Pin_2, Part1.D8
  N11: Part3.VOUT, Part1.VIN
  N12: Part3.VIN, VCC2.+

notes:
  Fun with Arduino by Rob Purser is licensed under a
  Creative Commons
  Attribution-NonCommercial-ShareAlike 3.0 Unported License.
  Based on a work at http://www.funwitharduino.net/
  Copyright 2013-2014, Rob Purser
  Fun with Arduino by Rob Purser is licensed under a
  Creative Commons
  Attribution-NonCommercial-ShareAlike 3.0 Unported License.
  Based on a work at https://sites.google.com/site/funarduino/
  Copyright 2013, Rob Purser
  Note that this is connected to 3.3V!
  Don't connect this white wire when the USB is connected.
  The battery box has a power switch!
