# Fritzing sketch Cheerlights (saved by Fritzing 0.9.0b)
breadboards: 1

parts:
  R1 = Resistor [tolerance=±5% resistance=330 package=THT]
  R2 = Resistor [tolerance=±5% resistance=330 package=THT]
  R3 = Resistor [tolerance=±5% resistance=330 package=THT]
  LED1 = RGB LED - (4 legs) [package="5 mm [THT]"]
  part = Arduino Uno (Rev3)  # not connected
  Arduino1 = Arduino Uno (Rev3)

nets:
  N1: R1.Pin_0, LED1.red_cathode
  N2: R1.Pin_1, Arduino1.D9_PWM
  N3: R2.Pin_0, LED1.green_cathode
  N4: R2.Pin_1, Arduino1.D6_PWM
  N5: R3.Pin_0, LED1.blue_cathode
  N6: R3.Pin_1, Arduino1.D5_PWM
  GND: LED1.common_anode, Arduino1.GND

notes:
  Fun with Arduino by Rob Purser is licensed under a
  Creative Commons
  Attribution-NonCommercial-ShareAlike 3.0 Unported License.
  Based on a work at http://www.funwitharduino.net
  Copyright 2013-2014, Rob Purser
